# Fritzing sketch wiring-diagram (saved by Fritzing 0.9.10b)
circuit board: 8.46667cm x 5.64444cm
perfboards: 2

parts:
  Mod1 = Raspberry Pi Pico W
  M1 = BTS7960
  Part1 = Triple Axis Accelerometer Breakout - ADXL345
  U1 = Vibration Motor- ROB-08449 [package=vibe-motor-10mm]
  S1 = Momentary Switch [package=tactile-pth]
  S2 = Momentary Switch [package=tactile-pth]
  S3 = Momentary Switch [package=tactile-pth]
  S4 = Momentary Switch [package=tactile-pth]
  S5 = Momentary Switch [package=tactile-pth]
  SW1 = ENCODER_RGB_CA [package=encoder_led_3]
  SW2 = ENCODER_RGB_CA [package=encoder_led_3]
  M3 = RioRand LM2596
  J2 = Power Jack [package=power_jack_combo]
  U2 = SWITCH-SPST-2 [package=r_sw_th]
  Grove1 = Grove OLED 128x96
  J3 = Piezo Speaker
  M2 = DC Motor [voltage_(max)=6V voltage_(min)=3V]  # not connected

nets:
  N1: Mod1.pin_1, M1.pin1
  N2: Mod1.pin_2, M1.pin2
  GND: Mod1.pin_3, Mod1.pin_28, Mod1.pin_38, M1.pin8, Part1.GND, U1.+, S1.3, S2.3, S3.3, S4.3, S5.3, SW1.B, SW2.B, M3.Pin_4, Grove1.GND, J3.pin1
  N3: Mod1.pin_6, Grove1.SCL
  N4: Mod1.pin_7, Grove1.SDA
  N5: Mod1.pin_9, Part1.SDA
  N6: Mod1.pin_10, Part1.SCL
  N7: Mod1.pin_12, S3.1
  N8: Mod1.pin_14, S4.1
  N9: Mod1.pin_15, S5.1
  N10: Mod1.pin_17, SW1.-B
  N11: Mod1.pin_19, SW1.A
  N12: Mod1.pin_20, SW1.+
  N13: Mod1.pin_21, U1.-
  N14: Mod1.pin_26, SW2.+
  N15: Mod1.pin_27, SW2.A
  N16: Mod1.pin_31, S1.1
  N17: Mod1.pin_32, S2.1
  N18: Mod1.pin_34, J3.pin2
  N19: Mod1.pin_39, M1.pin3, M1.pin4, M1.pin7, Part1.VCC, SW2.C, M3.Pin_3
  N20: M1.pin11, M3.Pin_1, U2.O
  N21: M1.pin12, M3.Pin_2, J2.GNDBREAK
  N22: SW1.C, Grove1.VCC
  N23: J2.PWR, U2.P

notes:
  orange clk
  gray dt
  white sw
  green clk
  blue dt
  up
  down
  1
  2
  3

custom parts:
  Raspberry Pi Pico W: Raspberry Pi Pico W. Based around the RP2040 microcontroller the Pico W is a low cost microcontroller device bringing Raspberry Pi quality, cost, and easy of use to the microcontroller space. The areas marked KEEPOUT in pcb silkscreen should not have traces running through them to avoid shorts on a soldered in module!
  BTS7960: BTS7960 43A Peak Power H-Bridge PWM Motor Driver
